# Fritzing sketch pi_leds (saved by Fritzing 0.9.3b)
breadboards: 1

parts:
  Raspberry_Pi_1 = Raspberry Pi 3 [part_number=RPI-3-V1.2]
  LED3 = LED - 3mm [color="Red (633nm)" package="3 mm [THT]"]
  LED4 = LED - 3mm [color="Red (633nm)" package="3 mm [THT]"]
  R1 = Resistor [tolerance=±5% resistance=220 package="0805 [SMD]"]
  R2 = Resistor [tolerance=±5% resistance=220 package="0805 [SMD]"]
  R3 = Resistor [tolerance=±5% resistance=220 package="0805 [SMD]"]
  R4 = Resistor [tolerance=±5% resistance=220 package="0805 [SMD]"]
  LED5 = LED - 3mm [color="Red (633nm)" package="3 mm [THT]"]
  LED6 = LED - 3mm [color="Red (633nm)" package="3 mm [THT]"]

nets:
  N1: Raspberry_Pi_1.GIPO21, LED6.cathode
  N2: Raspberry_Pi_1.GIPO12, LED5.anode
  N3: Raspberry_Pi_1.GIPO24, LED3.anode
  N4: Raspberry_Pi_1.GIPO18, LED4.anode
  N5: Raspberry_Pi_1.GND, R1.Pin_1, R2.Pin_1, R3.Pin_1, R4.Pin_1
  N6: LED3.cathode, R2.Pin_0
  N7: LED4.cathode, R1.Pin_0
  N8: R3.Pin_0, LED5.cathode
  N9: R4.Pin_0, LED6.anode
